# Fritzing sketch Untitled Sketch (saved by Fritzing 0.9.10b)
circuit board: 2.68907cm x 5.99524cm
breadboards: 1

parts:
  Part4 = Adafruit Feather M0 Express [part_number="Adafruit #3403"]
  Part1 = Arduino Nano (Rev3.0)

nets:
  GND: Part4.GND, Part1.GND
  N1: Part4.TX, Part1.D0/RX
  N2: Part4.RX, Part1.D1/TX

custom parts:
  Adafruit Feather M0 Express: We love all our Feathers equally, but this Feather is very special. It's our first Feather that is specifically designed for use with CircuitPython! CircuitPython is our beginner-oriented flavor of MicroPython - and as the name hints at, its a small but full-featured version of the popular Python programming language specifically for use with circuitry and electronics. That doesn't mean you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
